# Fritzing sketch schematic (saved by Fritzing 0.9.3b)
circuit board: 8.46667cm x 5.64444cm

parts:
  START = Round Pushbutton
  R1 = Resistor [tolerance=±5% resistance=4.7k package=THT]
  Part1 = Arduino Nano (Rev3.0)
  STOP = Round Pushbutton
  R2 = Resistor [tolerance=±5% resistance=4.7k package=THT]
  R3 = Resistor [tolerance=±5% resistance=220 package=THT]
  F2 = Rotary Potentiometer (Small) [maximum_resistance=100kΩ package=THT]
  P2 = Rotary Potentiometer (Small) [maximum_resistance=100kΩ package=THT]
  P1 = Rotary Potentiometer (Small) [maximum_resistance=100kΩ package=THT]
  F1 = Rotary Potentiometer (Small) [maximum_resistance=100kΩ package=THT]
  R1_2 = RELAY [package=relay-g5q]
  R2_2 = RELAY [package=relay-g5q]
  R4 = Resistor [tolerance=±5% resistance=220 package=THT]
  F2_2 = LED - 5mm [color="Red (633nm)" package="5 mm [THT]"]
  R5 = Resistor [tolerance=±5% resistance=220 package=THT]
  R11 = Resistor [tolerance=±5% resistance=220 package=THT]
  R12 = Resistor [tolerance=±5% resistance=220 package=THT]
  R13 = Resistor [tolerance=±5% resistance=220 package=THT]
  R14 = Resistor [tolerance=±5% resistance=220 package=THT]
  R15 = Resistor [tolerance=±5% resistance=220 package=THT]
  F2_3 = LED - 5mm [color="Red (633nm)" package="5 mm [THT]"]
  P2_2 = LED - 5mm [color="Orange (620nm)" package="5 mm [THT]"]
  F2_1 = LED - 5mm [color="Red (633nm)" package="5 mm [THT]"]
  P1_2 = LED - 5mm [color="Orange (620nm)" package="5 mm [THT]"]
  F1_2 = LED - 5mm [color="Red (633nm)" package="5 mm [THT]"]
  STOP_2 = LED - 5mm [color="Red (633nm)" package="5 mm [THT]"]
  ON/OFF = LED - 5mm [color="Green (570nm)" package="5 mm [THT]"]

nets (from the schematic view):
  N1: START.leg0, Part1.5V, STOP.leg0
  N2: START.leg1, R1.Pin_1, Part1.D2
  N3: R1.Pin_0, Part1.GND, R2.Pin_0, F2.leg1, P2.leg1, P1.leg1, F1.leg1, R1_2.COIL2, R2_2.COIL2, F2_2.cathode, F2_3.cathode, P2_2.cathode, F2_1.cathode, P1_2.cathode, F1_2.cathode, STOP_2.cathode, ON/OFF.cathode
  N4: Part1.D3, STOP.leg1, R2.Pin_1
  N5: Part1.D4, R1_2.COIL1
  N6: Part1.D5, R2_2.COIL1
  N7: Part1.D6, R3.Pin_1
  N8: Part1.D7, R15.Pin_0
  N9: Part1.D8, R12.Pin_0
  N10: Part1.D9, R11.Pin_0
  N11: Part1.D10, R5.Pin_0
  N12: Part1.D11/MOSI, R4.Pin_0
  N13: Part1.D12/MISO, R13.Pin_0
  N14: Part1.A3, P2.wiper
  N15: Part1.A2, F2.wiper
  N16: Part1.A1, P1.wiper
  N17: Part1.A0, F1.wiper
  N18: Part1.D13/SCK, R14.Pin_0
  N19: R3.Pin_0, ON/OFF.anode
  N20: F2.leg2, P2.leg2, P1.leg2, F1.leg2
  N21: R4.Pin_1, F2_2.anode
  N22: R5.Pin_1, F2_1.anode
  N23: R11.Pin_1, P1_2.anode
  N24: R12.Pin_1, F1_2.anode
  N25: R13.Pin_1, F2_3.anode
  N26: R14.Pin_1, P2_2.anode
  N27: R15.Pin_1, STOP_2.anode
